// Logisim project addbass.circ as structural Verilog: 1 circuit, main circuit main
module main (
);

  wire and_1_out, and_2_out, and_3_out, and_4_out, clock_1_out, decoder_1_out0, decoder_1_out1,
       decoder_1_out2, decoder_1_out3, myClock_out, not_1_out, not_2_out;
  wire [7:0] adder_1_out, adder_2_out, multiplexer_1_out, multiplexer_2_out, multiplexer_3_out,
       multiplexer_4_out, PC_q, ram_2_dout, register_1_q, register_2_q, register_3_q, register_4_q,
       subtractor_1_out;
  wire [15:0] ram_1_dout;

  Clock myClock (.out(myClock_out));
  Register PC (.D(adder_1_out), .clk(myClock_out), .Q(PC_q));  // open: en, clr
  Adder adder_1 (.a(PC_q), .b(8'h1), .out(adder_1_out));  // open: cin, cout
  RAM #(.dataWidth(16)) ram_1 (.addr(PC_q), .we(1'b0), .oe(1'b1), .clk(myClock_out), .dout(ram_1_dout));  // open: din
  Decoder #(.select(2)) decoder_1 (
    .out0(decoder_1_out0), .out1(decoder_1_out1), .out2(decoder_1_out2), .out3(decoder_1_out3),
    .sel(ram_1_dout[1:0]));  // open: en
  not not_1 (not_1_out, myClock_out);
  and and_1 (and_1_out, ram_1_dout[12], decoder_1_out0);
  and and_2 (and_2_out, ram_1_dout[12], decoder_1_out1);
  and and_3 (and_3_out, ram_1_dout[12], decoder_1_out2);
  and and_4 (and_4_out, ram_1_dout[12], decoder_1_out3);
  Register register_1 (.D(multiplexer_4_out), .en(and_1_out), .clk(not_1_out), .Q(register_1_q));  // open: clr
  Register register_2 (.D(multiplexer_4_out), .en(and_2_out), .clk(not_1_out), .Q(register_2_q));  // open: clr
  Register register_3 (.D(multiplexer_4_out), .en(and_3_out), .clk(not_1_out), .Q(register_3_q));  // open: clr
  Register register_4 (.D(multiplexer_4_out), .en(and_4_out), .clk(not_1_out), .Q(register_4_q));  // open: clr
  Multiplexer #(.select(2), .width(8)) multiplexer_1 (
    .in0(register_1_q), .in1(register_2_q), .in2(register_3_q), .in3(register_4_q), .out(multiplexer_1_out),
    .sel(ram_1_dout[3:2]));
  Subtractor subtractor_1 (.a(multiplexer_1_out), .b(ram_1_dout[11:4]), .out(subtractor_1_out));  // open: bin, bout
  Adder adder_2 (.a(multiplexer_1_out), .b(ram_1_dout[11:4]), .out(adder_2_out));  // open: cin, cout
  Multiplexer #(.select(2), .width(8)) multiplexer_2 (
    .in0(register_1_q), .in1(register_2_q), .in2(register_3_q), .in3(register_4_q), .out(multiplexer_2_out),
    .sel(ram_1_dout[1:0]));
  Multiplexer #(.width(8)) multiplexer_3 (
    .in0(subtractor_1_out), .in1(adder_2_out), .out(multiplexer_3_out), .sel(ram_1_dout[13]));
  Clock clock_1 (.out(clock_1_out));
  not not_2 (not_2_out, clock_1_out);
  RAM ram_2 (
    .addr(multiplexer_3_out), .we(ram_1_dout[14]), .oe(1'b1), .clk(not_2_out), .din(multiplexer_2_out),
    .dout(ram_2_dout));
  Multiplexer #(.width(8)) multiplexer_4 (
    .in0(multiplexer_3_out), .in1(ram_2_dout), .out(multiplexer_4_out), .sel(ram_1_dout[15]));

  // Notes on the sheet:
  //   ADD BASS CPU
  //   NAME: Jordan Tam
  //   PLEDGE: I pledge my honor that I have abided by the Stevens Honor System.
  //   INSTRUCTION MEMORY
  //   RegWrite
  //   WriteReg
  //   RegDataW
  //   ReadReg
  //   RegData
endmodule
